# Fritzing sketch esp8266_ADNS3080_reflectivity_finder (saved by Fritzing 0.9.3b)
circuit board: 7.5cm x 5cm
breadboards: 1

parts:
  nodeMCU = NodeMCU V1.0
  ADNS3080 = female pin header, 10 pins [form="♀ (female)"]
  J1 = female pin header, 15 pins [form="♀ (female)"]
  J2 = female pin header, 15 pins [form="♀ (female)"]
  laser = female pin header, 2 pins [form="♀ (female)"]
  R1 = Resistor [tolerance=±5% resistance=220 package=THT]
  LED1 = LED - 5mm [color="Red (633nm)" package="5 mm [THT]"]
  LED2 = LED - 5mm [color="Red (633nm)" package="5 mm [THT]"]
  J3 = female pin header, 15 pins [form="♀ (female)"]
  J4 = female pin header, 15 pins [form="♀ (female)"]

nets:
  N1: nodeMCU.D1, laser.pin1
  N2: nodeMCU.3V3, ADNS3080.pin3, J4.pin1
  N3: nodeMCU.GND, ADNS3080.pin1, laser.pin2, LED1.cathode, LED2.cathode, J4.pin2
  N4: nodeMCU.D5, ADNS3080.pin7, J4.pin8
  N5: nodeMCU.D6, ADNS3080.pin5
  N6: nodeMCU.D7, ADNS3080.pin6
  N7: ADNS3080.pin4, J1.pin13, J4.pin13
  N8: J1.pin3, J4.pin3
  N9: J1.pin4, J4.pin4
  N10: J1.pin5, J4.pin5
  N11: J1.pin6, J4.pin6
  N12: J1.pin7, J4.pin7
  N13: J1.pin9, J4.pin9
  N14: J1.pin10, J4.pin10
  N15: J1.pin11, J4.pin11
  N16: J1.pin12, J4.pin12
  N17: J1.pin14, R1.Pin_0, J4.pin14
  N18: J1.pin15, J4.pin15
  N19: J2.pin1, J3.pin1
  N20: J2.pin2, J3.pin2
  N21: J2.pin3, J3.pin3
  N22: J2.pin4, J3.pin4
  N23: J2.pin5, J3.pin5
  N24: J2.pin6, J3.pin6
  N25: J2.pin7, J3.pin7
  N26: J2.pin8, J3.pin8
  N27: J2.pin9, J3.pin9
  N28: J2.pin10, J3.pin10
  N29: J2.pin11, J3.pin11
  N30: J2.pin12, J3.pin12
  N31: J2.pin13, J3.pin13
  N32: J2.pin14, J3.pin14
  N33: J2.pin15, J3.pin15
  N34: R1.Pin_1, LED1.anode, LED2.anode

notes:
  Laser Rangefinder
  ADNS3080
  prototype v0.1

custom parts:
  NodeMCU V1.0: ESP8266 based NodeMCU
